# Fritzing sketch Robot_Autonomo_ESP32 (saved by Fritzing 0.9.3b)

parts:
  ESP32_DevKit_V1 = DOIT Esp32 DevKit v1 (30 pins long, 11 pins width)
  TB6612FNG = SparkFun Motor Driver TB6612FNG (v11)
  Motor_A_(TT) = Motor TT (Getriebemotor)
  Motor_B_(TT) = Motor TT (Getriebemotor)
  Portabaterias_2x18650 = 18650 battery holder [package=battery-18650-kit]
  LM2596_(5_V) = Buck Convertor [package=THT]
  R_33k_(bateria-D34) = Resistencia 33kΩ
  R_10k_(D34-GND) = Resistencia 10kΩ
  R_1k_STBY = Resistencia 1kΩ
  Sensor_Derecho = HY-SRF05
  R_1k_ECHO_Derecho_(a) = Resistencia 1kΩ
  R_1k_ECHO_Derecho_(b) = Resistencia 1kΩ
  R_220_ECHO_Derecho = Resistencia 220Ω
  Sensor_Izquierdo = HY-SRF05
  R_1k_ECHO_Izquierdo_(a) = Resistencia 1kΩ
  R_1k_ECHO_Izquierdo_(b) = Resistencia 1kΩ
  R_220_ECHO_Izquierdo = Resistencia 220Ω
  Sensor_Frontal = HY-SRF05
  R_1k_ECHO_Frontal_(a) = Resistencia 1kΩ
  R_1k_ECHO_Frontal_(b) = Resistencia 1kΩ
  R_220_ECHO_Frontal = Resistencia 220Ω

nets:
  3V3: ESP32_DevKit_V1.3V3, TB6612FNG.VCC
  GND: ESP32_DevKit_V1.GND, TB6612FNG.GND, LM2596_(5_V).Negative_Output, R_10k_(D34-GND).Pin_2, R_1k_STBY.Pin_1, Sensor_Derecho.Pin_5, R_220_ECHO_Derecho.Pin_1, Sensor_Izquierdo.Pin_5, R_220_ECHO_Izquierdo.Pin_1, Sensor_Frontal.Pin_5, R_220_ECHO_Frontal.Pin_1
  N1: ESP32_DevKit_V1.D4, TB6612FNG.STBY, R_1k_STBY.Pin_2
  N2: ESP32_DevKit_V1.D5, Sensor_Frontal.Pin_2
  N3: ESP32_DevKit_V1.D18, R_1k_ECHO_Frontal_(a).Pin_2, R_1k_ECHO_Frontal_(b).Pin_2
  N4: ESP32_DevKit_V1.D19, Sensor_Izquierdo.Pin_2
  N5: ESP32_DevKit_V1.D21, R_1k_ECHO_Izquierdo_(a).Pin_2, R_1k_ECHO_Izquierdo_(b).Pin_2
  N6: ESP32_DevKit_V1.D22, Sensor_Derecho.Pin_2
  N7: ESP32_DevKit_V1.D23, R_1k_ECHO_Derecho_(a).Pin_2, R_1k_ECHO_Derecho_(b).Pin_2
  N8: ESP32_DevKit_V1.D34, R_33k_(bateria-D34).Pin_2, R_10k_(D34-GND).Pin_1
  N9: ESP32_DevKit_V1.D32, TB6612FNG.BIN2
  N10: ESP32_DevKit_V1.D25, TB6612FNG.PWMA
  N11: ESP32_DevKit_V1.D26, TB6612FNG.AIN1
  N12: ESP32_DevKit_V1.D27, TB6612FNG.AIN2
  N13: ESP32_DevKit_V1.D14, TB6612FNG.BIN1
  N14: ESP32_DevKit_V1.D13, TB6612FNG.PWMB
  N15: ESP32_DevKit_V1.VIN, TB6612FNG.VM, LM2596_(5_V).Positive_Output, Sensor_Derecho.Pin_1, Sensor_Izquierdo.Pin_1, Sensor_Frontal.Pin_1
  N16: TB6612FNG.B01, Motor_B_(TT).pin_1
  N17: TB6612FNG.B02, Motor_B_(TT).pin_2
  N18: TB6612FNG.A02, Motor_A_(TT).pin_2
  N19: TB6612FNG.A01, Motor_A_(TT).pin_1
  N20: Portabaterias_2x18650.+, LM2596_(5_V).Positive_Input, R_33k_(bateria-D34).Pin_1
  N21: Portabaterias_2x18650.-, LM2596_(5_V).Negative_Input
  N22: Sensor_Derecho.Pin_3, R_1k_ECHO_Derecho_(a).Pin_1
  N23: R_1k_ECHO_Derecho_(b).Pin_1, R_220_ECHO_Derecho.Pin_2
  N24: Sensor_Izquierdo.Pin_3, R_1k_ECHO_Izquierdo_(a).Pin_1
  N25: R_1k_ECHO_Izquierdo_(b).Pin_1, R_220_ECHO_Izquierdo.Pin_2
  N26: Sensor_Frontal.Pin_3, R_1k_ECHO_Frontal_(a).Pin_1
  N27: R_1k_ECHO_Frontal_(b).Pin_1, R_220_ECHO_Frontal.Pin_2

custom parts:
  DOIT Esp32 DevKit v1 (30 pins long, 11 pins width): The DOIT Esp32 DevKit v1 is one of the development board created by DOIT to evaluate the ESP-WROOM-32 module. It is based on the ESP32 microcontroller that boasts Wifi, Bluetooth, Ethernet and Low Power support all in a single chip. (vanepp) made breadboard work, adjusted pin numbering and labels and reduced size of schematic and cleaned up pcb. This chip is 30pins long (2 x15) and 11 pins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
  SparkFun Motor Driver TB6612FNG (v11): The TB6612FNG Motor Driver can control up to two DC motors at a constant current of 1.2A (3.2A peak). Two input signals (IN1 and IN2) can be used to control the motor in one of four function modes: CW, CCW, short-brake and stop. The two motor outputs (A and B) can be separately controlled, and the speed of each motor is controlled via a PWM input signal with a frequency up to 100kHz. The STBY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
  Motor TT (Getriebemotor): Motor DC con reductor (TT). Version corregida de Getriebemotor.fzpz con vistas de esquema y PCB validas.
  18650 battery holder: 18650 Battery Holder
  Buck Convertor: DC to DC buck convertor
  Resistencia 33kΩ: Resistencia de 33k ohm, 1/4 W, THT.
  Resistencia 10kΩ: Resistencia de 10k ohm, 1/4 W, THT.
  Resistencia 1kΩ: Resistencia de 1k ohm, 1/4 W, THT.
  HY-SRF05: HY-SRF05 5Pin Distance Sensor.
  Resistencia 220Ω: Resistencia de 220 ohm, 1/4 W, THT.
